// Logisim project 16bitSingleCycleMIPS.circ as structural Verilog: 4 circuits, main circuit main
module main (
  input  in_1,
  input  in_2,
  input  [15:0] in_3,
  output [15:0] out_4,
  output [15:0] out_5,
  output [15:0] out_6,
  output [15:0] out_7,
  output [15:0] out_8,
  output [15:0] out_9,
  output [3:0] out_10,
  output [31:0] out_11,
  output [15:0] out_12
);

  wire alu_1_zero, and_1_out, CLK, controllerk_1_alumux, controllerk_1_branch, controllerk_1_datatoreg,
       controllerk_1_datawrite, controllerk_1_jump, controllerk_1_regaddress, controllerk_1_regwrite,
       not_1_out;
  wire [2:0] controllerk_1_out_10;
  wire [15:0] adder_1_out, adder_2_out, controlled_buffer_1_out, multiplexer_1_out, multiplexer_2_out,
       multiplexer_4_out;

  Multiplexer #(.width(16), .enable("false")) multiplexer_1 (
    .in0(adder_1_out), .in1(adder_2_out), .out(multiplexer_1_out), .sel(and_1_out));
  Multiplexer #(.width(16), .enable("false")) multiplexer_2 (
    .in0(multiplexer_1_out), .in1(out_6), .out(multiplexer_2_out), .sel(controllerk_1_jump));
  Register #(.width(16)) register_1 (.D(multiplexer_2_out), .en(1'b1), .Q(out_5), .clk(CLK), .clr(in_2));
  Adder #(.width(16)) adder_1 (.a(out_5), .b(in_3), .out(adder_1_out));  // open: cin, cout
  Adder #(.width(16)) adder_2 (.a(adder_1_out), .b(out_6), .out(adder_2_out));  // open: cin, cout
  ROM #(.addrWidth(16), .dataWidth(32)) rom_1 (.addr(out_5), .data({out_11[31:16], out_6}), .sel(in_1));
  _16RegFile u_16regfile_1 (
    .A1(out_11[24:21]), .A3(out_10), .A2(out_11[19:16]), .WD3(out_9), .out_7(out_8), .out_8(out_12),
    .in_6(controllerk_1_regwrite), .in_5(CLK));
  ControllerK controllerk_1 (
    .OPCode(out_11[31:26]), .Funct(out_6[5:0]), .Jump(controllerk_1_jump),
    .DataToReg(controllerk_1_datatoreg), .DataWrite(controllerk_1_datawrite), .Branch(controllerk_1_branch),
    .ALUmux(controllerk_1_alumux), .RegAddress(controllerk_1_regaddress), .RegWrite(controllerk_1_regwrite),
    .out_10(controllerk_1_out_10));
  Clock clock_1 (.out(CLK));
  Multiplexer #(.width(4), .enable("false")) multiplexer_3 (
    .in0(out_11[19:16]), .in1(out_6[14:11]), .out(out_10), .sel(controllerk_1_regaddress));
  Multiplexer #(.width(16), .enable("false")) multiplexer_4 (
    .in0(out_12), .in1(out_6), .out(multiplexer_4_out), .sel(controllerk_1_alumux));
  ALU alu_1 (
    .Data1(out_8), .AluControl(controllerk_1_out_10), .Data2(multiplexer_4_out), .out_4(out_4),
    .Zero(alu_1_zero));
  and and_1 (and_1_out, controllerk_1_branch, alu_1_zero);
  Multiplexer #(.width(16), .enable("false")) multiplexer_5 (
    .in0(out_4), .in1(controlled_buffer_1_out), .out(out_9), .sel(controllerk_1_datatoreg));
  assign controlled_buffer_1_out = controllerk_1_datawrite ? out_12 : 16'bz;  // Controlled_Buffer controlled_buffer_1
  not not_1 (not_1_out, controllerk_1_datawrite);
  RAM #(.addrWidth(16), .dataWidth(16)) ram_1 (
    .addr(out_4), .data(controlled_buffer_1_out), .clk(CLK), .ld(not_1_out));  // open: sel, clr

  assign out_7 = out_6;
  assign out_11[15:0] = out_6;

  // Other names for the same wires on the sheet: A3[3:0] = out_10; D[31:0] = {out_11[31:16], out_6};
  //   Data[15:0] = out_9; RD1[15:0] = out_8; RD2[15:0] = out_12

  // Notes on the sheet:
  //   jump
  //   contents of rom_1 (hex, n*v repeats v):
  //   40010020 40020018 20220006 22182a 20600002 411022 8000002 220822 8000002 402f0000 8000000
  //   FUNC
  //   OP
  //    RegWrite
  //   RegAddress
  //   AluMux
  //   ALUCont
  //   Branch
  //   DataWrite
  //   DataToReg
endmodule

module _16RegFile (
  input  [3:0] A1,
  input  [3:0] A3,
  input  [3:0] A2,
  input  [15:0] WD3,
  input  in_5,
  input  in_6,
  output [15:0] out_7,
  output [15:0] out_8
);

  wire and_1_out, and_2_out, and_3_out, and_4_out, and_5_out, and_6_out, and_7_out, and_8_out, and_9_out,
       and_10_out, and_11_out, and_12_out, and_13_out, and_14_out, and_15_out, and_16_out, decoder_1_out0,
       decoder_1_out1, decoder_1_out2, decoder_1_out3, decoder_1_out4, decoder_1_out5, decoder_1_out6,
       decoder_1_out7, decoder_1_out8, decoder_1_out9, decoder_1_out10, decoder_1_out11, decoder_1_out12,
       decoder_1_out13, decoder_1_out14, decoder_1_out15;
  wire [15:0] register_1_q, register_2_q, register_3_q, register_4_q, register_5_q, register_6_q,
       register_7_q, register_8_q, register_9_q, register_10_q, register_11_q, register_12_q, register_13_q,
       register_14_q, register_15_q, register_16_q;

  Decoder #(.select(4), .enable("false")) decoder_1 (
    .out0(decoder_1_out0), .out1(decoder_1_out1), .out2(decoder_1_out2), .out3(decoder_1_out3),
    .out4(decoder_1_out4), .out5(decoder_1_out5), .out6(decoder_1_out6), .out7(decoder_1_out7),
    .out8(decoder_1_out8), .out9(decoder_1_out9), .out10(decoder_1_out10), .out11(decoder_1_out11),
    .out12(decoder_1_out12), .out13(decoder_1_out13), .out14(decoder_1_out14), .out15(decoder_1_out15),
    .sel(A3));
  and and_1 (and_1_out, decoder_1_out0, in_6);
  and and_2 (and_2_out, decoder_1_out1, in_6);
  and and_3 (and_3_out, decoder_1_out2, in_6);
  and and_4 (and_4_out, decoder_1_out3, in_6);
  and and_5 (and_5_out, decoder_1_out4, in_6);
  and and_6 (and_6_out, decoder_1_out5, in_6);
  and and_7 (and_7_out, decoder_1_out6, in_6);
  and and_8 (and_8_out, decoder_1_out7, in_6);
  Register #(.width(16)) register_1 (.D(WD3), .en(and_1_out), .Q(register_1_q), .clk(in_5));  // open: clr
  Register #(.width(16)) register_2 (.D(WD3), .en(and_2_out), .Q(register_2_q), .clk(in_5));  // open: clr
  Register #(.width(16)) register_3 (.D(WD3), .en(and_3_out), .Q(register_3_q), .clk(in_5));  // open: clr
  Register #(.width(16)) register_4 (.D(WD3), .en(and_4_out), .Q(register_4_q), .clk(in_5));  // open: clr
  Register #(.width(16)) register_5 (.D(WD3), .en(and_5_out), .Q(register_5_q), .clk(in_5));  // open: clr
  Register #(.width(16)) register_6 (.D(WD3), .en(and_6_out), .Q(register_6_q), .clk(in_5));  // open: clr
  Register #(.width(16)) register_7 (.D(WD3), .en(and_7_out), .Q(register_7_q), .clk(in_5));  // open: clr
  Register #(.width(16)) register_8 (.D(WD3), .en(and_8_out), .Q(register_8_q), .clk(in_5));  // open: clr
  and and_9 (and_9_out, decoder_1_out8, in_6);
  and and_10 (and_10_out, decoder_1_out9, in_6);
  and and_11 (and_11_out, decoder_1_out10, in_6);
  and and_12 (and_12_out, decoder_1_out11, in_6);
  and and_13 (and_13_out, decoder_1_out12, in_6);
  and and_14 (and_14_out, decoder_1_out13, in_6);
  and and_15 (and_15_out, decoder_1_out14, in_6);
  and and_16 (and_16_out, decoder_1_out15, in_6);
  Register #(.width(16)) register_9 (.D(WD3), .en(and_9_out), .Q(register_9_q), .clk(in_5));  // open: clr
  Register #(.width(16)) register_10 (.D(WD3), .en(and_10_out), .Q(register_10_q), .clk(in_5));  // open: clr
  Register #(.width(16)) register_11 (.D(WD3), .en(and_11_out), .Q(register_11_q), .clk(in_5));  // open: clr
  Register #(.width(16)) register_12 (.D(WD3), .en(and_12_out), .Q(register_12_q), .clk(in_5));  // open: clr
  Register #(.width(16)) register_13 (.D(WD3), .en(and_13_out), .Q(register_13_q), .clk(in_5));  // open: clr
  Register #(.width(16)) register_14 (.D(WD3), .en(and_14_out), .Q(register_14_q), .clk(in_5));  // open: clr
  Register #(.width(16)) register_15 (.D(WD3), .en(and_15_out), .Q(register_15_q), .clk(in_5));  // open: clr
  Register #(.width(16)) register_16 (.D(WD3), .en(and_16_out), .Q(register_16_q), .clk(in_5));  // open: clr
  Multiplexer #(.select(4), .width(16), .enable("false")) multiplexer_1 (
    .in0(register_1_q), .in1(register_2_q), .in2(register_3_q), .in3(register_4_q), .in4(register_5_q),
    .in5(register_6_q), .in6(register_7_q), .in7(register_8_q), .in8(register_9_q), .in9(register_10_q),
    .in10(register_11_q), .in11(register_12_q), .in12(register_13_q), .in13(register_14_q),
    .in14(register_15_q), .in15(register_16_q), .out(out_7), .sel(A1));
  Multiplexer #(.select(4), .width(16), .enable("false")) multiplexer_2 (
    .in0(register_1_q), .in1(register_2_q), .in2(register_3_q), .in3(register_4_q), .in4(register_5_q),
    .in5(register_6_q), .in6(register_7_q), .in7(register_8_q), .in8(register_9_q), .in9(register_10_q),
    .in10(register_11_q), .in11(register_12_q), .in12(register_13_q), .in13(register_14_q),
    .in14(register_15_q), .in15(register_16_q), .out(out_8), .sel(A2));

  // Other names for the same wires on the sheet: clk = in_5; RegWrite = in_6
endmodule

module ALU (
  input  [15:0] Data1,
  input  [2:0] AluControl,
  input  [15:0] Data2,
  output [15:0] out_4,
  output Zero
);

  wire comparator_1_lt;
  wire [15:0] adder_1_out, and_1_out, bit_extender_1_out, or_1_out, subtractor_1_out;

  Adder #(.width(16)) adder_1 (.a(Data1), .b(Data2), .out(adder_1_out));  // open: cin, cout
  Subtractor #(.width(16)) subtractor_1 (.a(Data1), .b(Data2), .out(subtractor_1_out));  // open: bin, bout
  assign or_1_out = Data1 | Data2;  // OR_Gate or_1, 16 bits wide
  assign and_1_out = Data1 & Data2;  // AND_Gate and_1, 16 bits wide
  Comparator #(.width(16)) comparator_1 (.a(Data1), .b(Data2), .eq(Zero), .lt(comparator_1_lt));  // open: gt
  Multiplexer #(.select(3), .width(16), .enable("false")) multiplexer_1 (
    .in0(and_1_out), .in1(or_1_out), .in2(adder_1_out), .in6(subtractor_1_out), .in7(bit_extender_1_out),
    .out(out_4), .sel(AluControl));  // open: in3, in4, in5
  assign bit_extender_1_out = {{15{1'b0}}, comparator_1_lt};  // Bit_Extender bit_extender_1
endmodule

module ControllerK (
  input  [5:0] OPCode,
  input  [5:0] Funct,
  output Jump,
  output DataToReg,
  output DataWrite,
  output Branch,
  output ALUmux,
  output RegAddress,
  output RegWrite,
  output [2:0] out_10
);

  wire addf_out, and_1_out, and_2_out, and_3_out, and_4_out, and_5_out, and_6_out, and_7_out, and_8_out,
       andf_out, or_1_out, or_2_out, orf_out, sltf_out, subf_out;
  wire [1:0] not_2_out;
  wire [2:1] rom_1_data;
  wire [5:0] not_1_out;

  assign not_1_out = ~Funct;  // NOT_Gate not_1, 6 bits wide
  assign not_2_out = ~rom_1_data;  // NOT_Gate not_2, 2 bits wide
  ROM #(.addrWidth(6), .dataWidth(9)) rom_1 (
    .addr(OPCode), .data({RegWrite, RegAddress, ALUmux, Branch, DataWrite, DataToReg, rom_1_data, Jump}));  // open: sel
  and and_1 (and_1_out, not_2_out[0], rom_1_data[2]);
  and and_2 (and_2_out, not_2_out[0], not_2_out[1]);
  and addf (addf_out, not_1_out[0], not_1_out[1], not_1_out[2], not_1_out[3]);
  and subf (subf_out, not_1_out[3], not_1_out[2], Funct[1], not_1_out[0]);
  and andf (andf_out, not_1_out[0], not_1_out[1], not_1_out[3], Funct[2]);
  and orf (orf_out, Funct[0], not_1_out[1], Funct[2], not_1_out[3]);
  and sltf (sltf_out, not_1_out[2], Funct[1], not_1_out[0], Funct[3]);
  and and_3 (and_3_out, and_1_out, addf_out);
  and and_4 (and_4_out, and_1_out, subf_out);
  and and_5 (and_5_out, and_1_out, andf_out);
  and and_6 (and_6_out, and_1_out, orf_out);
  and and_7 (and_7_out, and_1_out, sltf_out);
  or or_1 (or_1_out, and_3_out, and_2_out);
  and and_8 (and_8_out, not_2_out[1], rom_1_data[1]);
  or or_2 (or_2_out, and_8_out, and_4_out);
  or or_3 (out_10[2], or_2_out, and_7_out);
  or or_4 (out_10[1], or_1_out, out_10[2]);
  or or_5 (out_10[0], and_6_out, and_7_out);

  // Notes on the sheet:
  //   contents of rom_1 (hex, n*v repeats v):
  //   184 0 1 0 11 0 0 0 22 7*0 140 18*0 148 7*0 50
  //   ALUOP
  //   and
  //   or
  //   slt
  //   add
  //   sub
endmodule
